// Digital circuit and-gate.dig as structural Verilog
module and_gate (
  input  A,
  input  B,
  output Y
);

  and and_1 (Y, A, B);
endmodule

/* Test case AND truth table:
A B Y
0 0 0
0 1 0
1 0 0
1 1 1
*/
