// Digital circuit half-adder.dig as structural Verilog
module half_adder (
  input  A,
  input  B,
  output S,
  output Cout
);

  xor xor_1 (S, A, B);
  and and_1 (Cout, A, B);
endmodule

/* Test case Half adder truth table:
A B S Cout
0 0 0 0
0 1 1 0
1 0 1 0
1 1 0 1
*/
