// Digital circuit sr-latch.dig as structural Verilog
module sr_latch (
  input  S,
  input  R,
  output Q,
  output nQ
);

  // NOr nor_1 has open pins: In_1=S, In_2=nQ, out=open
  // NOr nor_2 has open pins: In_1=Q, In_2=R, out=open
endmodule
